// Logisim project circuito_vetorial.circ as structural Verilog: 7 circuits, main circuit main
module main (
);

  wire adder_1_cout, and_1_out, Branch, CLK, comparator_1_gt, comparator_1_lt, Reset, S_WE, S_WR, Sel_H,
       V_WE, V_WR, W_SR1, W_VR1, Zero;
  wire [1:0] ALUOp, DataToReg, multiplexer_3_out, S_RA, S_RB, V_RA, V_RB, V_RD;
  wire [3:0] Imm, Opcode;
  wire [7:0] adder_1_out, MemDados_S_dout, MemInstrucao_data, multiplexer_1_out, multiplexer_4_out,
       multiplexer_5_out, multiplexer_6_out, multiplexer_7_out, multiplexer_8_out, PC_q, ram_1_dout,
       ram_2_dout, ram_3_dout, ram_4_dout, S_DRA, S_DRB, S_Mov, ula_1_s, ula_2_s, ula_3_s, ula_4_s, ula_5_s,
       V_DRA0, V_DRA1, V_DRA2, V_DRA3, V_DRB0, V_DRB1, V_DRB2, V_DRB3, V_Mov0, V_Mov1, V_Mov2, V_Mov3;

  Button button_1 (.out(Reset));
  Clock clock_1 (.out(CLK));
  Adder adder_1 (.a(PC_q), .b(8'h1), .out(adder_1_out), .cin(1'b0), .cout(adder_1_cout));
  LED led_1 (.in(adder_1_cout));
  and and_1 (and_1_out, Branch, Zero);
  ROM #(.addrWidth(4), .dataWidth(12)) MemControle (
    .addr(Opcode), .data({ALUOp, Branch, DataToReg, W_SR1, W_VR1, S_WR, V_WR, Sel_H, S_WE, V_WE}));
  // Probe on multiplexer_1_out
  Multiplexer #(.width(8)) multiplexer_1 (.in0(adder_1_out), .in1(S_DRB), .out(multiplexer_1_out), .sel(and_1_out));
  // Probe on V_RD
  Multiplexer #(.width(2)) multiplexer_2 (.in0(V_RA), .in1(2'b01), .out(V_RD), .sel(W_VR1));
  Register PC (.D(multiplexer_1_out), .en(1'b1), .clk(CLK), .Q(PC_q), .clr(Reset));
  // Probe on PC_q
  ROM MemInstrucao (.addr(PC_q), .data(MemInstrucao_data));
  // Probe on ALUOp
  // Probe on DataToReg
  // Probe on multiplexer_8_out
  Decodificador decodificador_1 (
    .Inst(MemInstrucao_data), .Imm(Imm), .S_RA(S_RA), .V_RA(V_RA), .S_RB(S_RB), .V_RB(V_RB), .Opcode(Opcode));
  // Probe on V_RB
  Multiplexer #(.width(2)) multiplexer_3 (.in0(S_RA), .in1(2'b01), .out(multiplexer_3_out), .sel(W_SR1));
  // Probe on multiplexer_3_out
  // Probe on S_RB
  BR_seq br_seq_1 (
    .Reset(Reset), .Clk(CLK), .Dados(multiplexer_8_out), .WriteReg(S_WR), .RW(multiplexer_3_out),
    .RA(multiplexer_3_out), .RB(S_RB), .DRA(S_DRA), .DRB(S_DRB));
  BR_vet br_vet_1 (
    .Reset(Reset), .Clk(CLK), .Dados(multiplexer_4_out), .VR0({8{1'b0}}), .WriteReg(V_WR), .RW(V_RD),
    .RA(V_RD), .RB(V_RB), .DRA(V_DRA0), .DRB(V_DRB0));
  // Probe on V_DRA0
  // Probe on V_DRB0
  BR_vet br_vet_2 (
    .Reset(Reset), .Clk(CLK), .Dados(multiplexer_5_out), .VR0(8'h1), .WriteReg(V_WR), .RW(V_RD), .RA(V_RD),
    .RB(V_RB), .DRA(V_DRA1), .DRB(V_DRB1));
  // Probe on V_DRA1
  // Probe on V_DRB1
  BR_vet br_vet_3 (
    .Reset(Reset), .Clk(CLK), .Dados(multiplexer_6_out), .VR0(8'h2), .WriteReg(V_WR), .RW(V_RD), .RA(V_RD),
    .RB(V_RB), .DRA(V_DRA2), .DRB(V_DRB2));
  // Probe on V_DRA2
  // Probe on V_DRB2
  BR_vet br_vet_4 (
    .Reset(Reset), .Clk(CLK), .Dados(multiplexer_7_out), .VR0(8'h3), .WriteReg(V_WR), .RW(V_RD), .RA(V_RD),
    .RB(V_RB), .DRA(V_DRA3), .DRB(V_DRB3));
  // Probe on V_DRA3
  // Probe on V_DRB3
  // Probe on S_DRA
  // Probe on S_DRB
  ULA ula_1 (.A(V_DRA0), .B(V_DRB0), .Funct(ALUOp), .S(ula_1_s));
  Mov mov_1 (.Imm(Imm), .R1(V_DRA0), .SelH(Sel_H), .S(V_Mov0));
  ULA ula_2 (.A(V_DRA1), .B(V_DRB1), .Funct(ALUOp), .S(ula_2_s));
  Mov mov_2 (.Imm(Imm), .R1(V_DRA1), .SelH(Sel_H), .S(V_Mov1));
  ULA ula_3 (.A(V_DRA2), .B(V_DRB2), .Funct(ALUOp), .S(ula_3_s));
  Mov mov_3 (.Imm(Imm), .R1(V_DRA2), .SelH(Sel_H), .S(V_Mov2));
  ULA ula_4 (.A(V_DRA3), .B(V_DRB3), .Funct(ALUOp), .S(ula_4_s));
  Mov mov_4 (.Imm(Imm), .R1(V_DRA3), .SelH(Sel_H), .S(V_Mov3));
  ULA ula_5 (.A(S_DRA), .B(S_DRB), .Funct(ALUOp), .S(ula_5_s));
  Mov mov_5 (.Imm(Imm), .R1(S_DRA), .SelH(Sel_H), .S(S_Mov));
  LED led_2 (.in(comparator_1_gt));
  Comparator comparator_1 (.a(S_DRA), .b({8{1'b0}}), .gt(comparator_1_gt), .eq(Zero), .lt(comparator_1_lt));
  LED led_3 (.in(comparator_1_lt));
  RAM #(.asyncread("true")) ram_1 (.addr(V_DRB0), .we(V_WE), .oe(1'b1), .clk(CLK), .din(V_DRA0), .dout(ram_1_dout));
  RAM #(.asyncread("true")) ram_2 (.addr(V_DRB1), .we(V_WE), .oe(1'b1), .clk(CLK), .din(V_DRA1), .dout(ram_2_dout));
  RAM #(.asyncread("true")) ram_3 (.addr(V_DRB2), .we(V_WE), .oe(1'b1), .clk(CLK), .din(V_DRA2), .dout(ram_3_dout));
  RAM #(.asyncread("true")) ram_4 (.addr(V_DRB3), .we(V_WE), .oe(1'b1), .clk(CLK), .din(V_DRA3), .dout(ram_4_dout));
  RAM MemDados_S (.addr(S_DRB), .we(S_WE), .oe(1'b1), .clk(CLK), .din(S_DRA), .dout(MemDados_S_dout));
  Multiplexer #(.select(2), .width(8)) multiplexer_4 (
    .in0(ula_1_s), .in1(ram_1_dout), .in2(V_Mov0), .out(multiplexer_4_out), .sel(DataToReg));  // open: in3
  Multiplexer #(.select(2), .width(8)) multiplexer_5 (
    .in0(ula_2_s), .in1(ram_2_dout), .in2(V_Mov1), .out(multiplexer_5_out), .sel(DataToReg));  // open: in3
  Multiplexer #(.select(2), .width(8)) multiplexer_6 (
    .in0(ula_3_s), .in1(ram_3_dout), .in2(V_Mov2), .out(multiplexer_6_out), .sel(DataToReg));  // open: in3
  Multiplexer #(.select(2), .width(8)) multiplexer_7 (
    .in0(ula_4_s), .in1(ram_4_dout), .in2(V_Mov3), .out(multiplexer_7_out), .sel(DataToReg));  // open: in3
  Multiplexer #(.select(2), .width(8)) multiplexer_8 (
    .in0(ula_5_s), .in1(MemDados_S_dout), .in2(S_Mov), .in3({8{1'b0}}), .out(multiplexer_8_out),
    .sel(DataToReg));
  // Probe on multiplexer_4_out
  // Probe on multiplexer_5_out
  // Probe on multiplexer_6_out
  // Probe on multiplexer_7_out
  // Probe on multiplexer_8_out

  // Notes on the sheet:
  //   contents of MemControle (hex, n*v repeats v):
  //   90 2 154 150 10 410 810 200 88 1 12c 128 8 408
  //   contents of MemInstrucao (hex, n*v repeats v):
  //   d5 da df 55 5a 5f c8 cc b4 33 49 37 21 79 9e c9 cd 31 20 59 3b 20 71 33 20 49 b8 cd b4 39 22 79 9e
  //   c9 cd 31 20 59 3d 21 71 33 20 49 df 38 23 79 9e c9 31 20 59 3d 22 71 33 20 49 da c8 3f 24 79 8e bc
  //   c9 86
  //   PE - Escalar
  //   PE - Vetorial
endmodule

module BR_seq (
  input  Reset,
  input  Clk,
  input  [7:0] Dados,
  input  WriteReg,
  input  [1:0] RW,
  input  [1:0] RA,
  input  [1:0] RB,
  output [7:0] DRA,
  output [7:0] DRB
);

  wire demultiplexer_1_out0, demultiplexer_1_out1, demultiplexer_1_out2, demultiplexer_1_out3;
  wire [7:0] SR1_q, SR2_q, SR3_q;

  Demultiplexer #(.select(2)) demultiplexer_1 (
    .out0(demultiplexer_1_out0), .out1(demultiplexer_1_out1), .out2(demultiplexer_1_out2),
    .out3(demultiplexer_1_out3), .in(WriteReg), .sel(RW));
  LED led_1 (.in(demultiplexer_1_out0));
  Register SR1 (.D(Dados), .en(demultiplexer_1_out1), .clk(Clk), .Q(SR1_q), .clr(Reset));
  Register SR2 (.D(Dados), .en(demultiplexer_1_out2), .clk(Clk), .Q(SR2_q), .clr(Reset));
  Register SR3 (.D(Dados), .en(demultiplexer_1_out3), .clk(Clk), .Q(SR3_q), .clr(Reset));
  Multiplexer #(.select(2), .width(8)) multiplexer_1 (
    .in0({8{1'b0}}), .in1(SR1_q), .in2(SR2_q), .in3(SR3_q), .out(DRA), .sel(RA));
  // Probe on DRA
  Multiplexer #(.select(2), .width(8)) multiplexer_2 (
    .in0({8{1'b0}}), .in1(SR1_q), .in2(SR2_q), .in3(SR3_q), .out(DRB), .sel(RB));
  // Probe on DRB
endmodule

module BR_vet (
  input  Reset,
  input  Clk,
  input  [7:0] Dados,
  input  [7:0] VR0,
  input  WriteReg,
  input  [1:0] RW,
  input  [1:0] RA,
  input  [1:0] RB,
  output [7:0] DRA,
  output [7:0] DRB
);

  wire demultiplexer_1_out0, demultiplexer_1_out1, demultiplexer_1_out2, demultiplexer_1_out3;
  wire [7:0] VR1_q, VR2_q, VR3_q;

  LED led_1 (.in(demultiplexer_1_out0));
  Demultiplexer #(.select(2)) demultiplexer_1 (
    .out0(demultiplexer_1_out0), .out1(demultiplexer_1_out1), .out2(demultiplexer_1_out2),
    .out3(demultiplexer_1_out3), .in(WriteReg), .sel(RW));
  Register VR1 (.D(Dados), .en(demultiplexer_1_out1), .clk(Clk), .Q(VR1_q), .clr(Reset));
  Register VR2 (.D(Dados), .en(demultiplexer_1_out2), .clk(Clk), .Q(VR2_q), .clr(Reset));
  Register VR3 (.D(Dados), .en(demultiplexer_1_out3), .clk(Clk), .Q(VR3_q), .clr(Reset));
  Multiplexer #(.select(2), .width(8)) multiplexer_1 (
    .in0(VR0), .in1(VR1_q), .in2(VR2_q), .in3(VR3_q), .out(DRA), .sel(RA));
  // Probe on DRA
  Multiplexer #(.select(2), .width(8)) multiplexer_2 (
    .in0(VR0), .in1(VR1_q), .in2(VR2_q), .in3(VR3_q), .out(DRB), .sel(RB));
  // Probe on DRB
endmodule

module ULA (
  input  [7:0] A,
  input  [7:0] B,
  input  [1:0] Funct,
  output [7:0] S
);

  wire adder_1_cout, subtractor_1_bout;
  wire [7:0] D0, D1, D2;

  Adder adder_1 (.a(A), .b(B), .out(D0), .cin(1'b0), .cout(adder_1_cout));
  Subtractor subtractor_1 (.a(A), .b(B), .out(D1), .bin(1'b0), .bout(subtractor_1_bout));
  assign D2 = A & B;  // AND_Gate and_1, 8 bits wide
  LED led_1 (.in(adder_1_cout));
  LED led_2 (.in(subtractor_1_bout));
  Multiplexer #(.select(2), .width(8)) multiplexer_1 (
    .in0(D0), .in1(D1), .in2(D2), .in3({8{1'b0}}), .out(S), .sel(Funct));

  // Notes on the sheet:
  //   A + B
  //   A - B
  //   A and B
endmodule

module Decodificador (
  input  [7:0] Inst,
  output [3:0] Imm,
  output [1:0] S_RA,
  output [1:0] V_RA,
  output [1:0] S_RB,
  output [1:0] V_RB,
  output [3:0] Opcode
);

  Demultiplexer #(.width(2)) demultiplexer_1 (.out0(S_RA), .out1(V_RA), .in(Inst[3:2]), .sel(Inst[7]));
  Demultiplexer #(.width(2)) demultiplexer_2 (.out0(S_RB), .out1(V_RB), .in(Inst[1:0]), .sel(Inst[7]));

  assign Imm = Inst[3:0];
  assign Opcode = Inst[7:4];
endmodule

module ExtensorSinal (
  input  [3:0] A,
  output [7:0] B
);


  assign B = {{5{A[3]}}, A[2:0]};
endmodule

module Mov (
  input  [3:0] Imm,
  input  [7:0] R1,
  input  SelH,
  output [7:0] S
);

  Multiplexer #(.width(8)) multiplexer_1 (.in0({R1[7:4], Imm}), .in1({Imm, R1[3:0]}), .out(S), .sel(SelH));

  // Other names for the same wires on the sheet: Mov_H[7:0] = {Imm, R1[3:0]}; R_low[3:0] = R1[3:0];
  //   Mov_L[7:0] = {R1[7:4], Imm}; R_High[3:0] = R1[7:4]
endmodule
